// Digital circuit control unit.dig as structural Verilog
module control_unit (
  input  [31:0] instr
);

  wire add, add_sub, addi, \and , andi, ecall_ibreak, funct3_2_eq, funct3_3_eq, funct3_4_eq, funct3_5_eq,
       funct3_6_eq, funct3_7_eq, funct3_8_eq, funct3_9_eq, funct3_10_eq, funct3_11_eq, funct3_12_eq,
       funct3_13_eq, funct3_14_eq, funct3_15_eq, funct3_16_eq, funct3_17_eq, funct3_18_eq, funct3_19_eq,
       funct3_20_eq, funct3_21_eq, funct3_22_eq, funct3_eq, funct7_eq, funct8_eq, i_arith, i_jalr, i_load,
       i_pc, imm_i_arith, jalr, lb, lbu, lh, lhu, lw, not_1_out, not_2_out, not_3_out, \or , ori, r, sll,
       slli, slr, slt, slti, sltiu, sltu, sra, srai, srl_sra, srli, srli_srai, sub, sub_sra, \xor , xori;
  wire [2:0] funct3_i_arith, funct3_i_jalr, funct3_i_load, funct3_i_pc, funct3_r;
  wire [6:0] funct7_r;
  wire [17:0] multiplexer_1_out;
  wire [24:0] multiplexer_2_out, multiplexer_3_out, multiplexer_4_out, multiplexer_5_out;

  Comparator #(.Bits(7)) type_r (.a(instr[6:0]), .b(7'b0110011), .eq(r));  // open: gt, lt
  Comparator #(.Bits(7)) type_i_arith (.a(instr[6:0]), .b(7'b0010011), .eq(i_arith));  // open: gt, lt
  Comparator #(.Bits(7)) type_i_load (.a(instr[6:0]), .b(7'b0000011), .eq(i_load));  // open: gt, lt
  Comparator #(.Bits(7)) type_i_jalr (.a(instr[6:0]), .b(7'b1100111), .eq(i_jalr));  // open: gt, lt
  Comparator #(.Bits(7)) type_i_pc (.a(instr[6:0]), .b(7'b1100111), .eq(i_pc));  // open: gt, lt
  Multiplexer #(.Bits(25)) multiplexer_1 (
    .sel(r), .in_0({25{1'b1}}), .in_1(instr[31:7]),
    .out({funct7_r, multiplexer_1_out[17:8], funct3_r, multiplexer_1_out[4:0]}));
  Multiplexer #(.Bits(25)) multiplexer_2 (
    .sel(i_arith), .in_0({25{1'b1}}), .in_1(instr[31:7]),
    .out({multiplexer_2_out[24], imm_i_arith, multiplexer_2_out[22:8], funct3_i_arith, multiplexer_2_out[4:0]}));
  Multiplexer #(.Bits(25)) multiplexer_3 (
    .sel(i_load), .in_0({25{1'b1}}), .in_1(instr[31:7]),
    .out({multiplexer_3_out[24:8], funct3_i_load, multiplexer_3_out[4:0]}));
  Multiplexer #(.Bits(25)) multiplexer_4 (
    .sel(i_jalr), .in_0({25{1'b1}}), .in_1(instr[31:7]),
    .out({multiplexer_4_out[24:8], funct3_i_jalr, multiplexer_4_out[4:0]}));
  Multiplexer #(.Bits(25)) multiplexer_5 (
    .sel(i_jalr), .in_0({25{1'b1}}), .in_1(instr[31:7]),
    .out({multiplexer_5_out[24:8], funct3_i_pc, multiplexer_5_out[4:0]}));
  Comparator #(.Bits(3)) funct3 (.a(funct3_r), .b(3'b000), .eq(funct3_eq));  // open: gt, lt
  Comparator #(.Bits(7)) funct7 (.a(funct7_r), .b(7'b0100000), .eq(funct7_eq));  // open: gt, lt
  Comparator #(.Bits(3)) funct3_2 (.a(funct3_i_arith), .b(3'b000), .eq(funct3_2_eq));  // open: gt, lt
  and and_1 (srai, imm_i_arith, i_arith, srli_srai);
  not not_1 (not_1_out, imm_i_arith);
  Comparator #(.Bits(3)) funct3_3 (.a(funct3_i_load), .b(3'b000), .eq(funct3_3_eq));  // open: gt, lt
  Comparator #(.Bits(3)) funct3_4 (.a(funct3_i_jalr), .b(3'b000), .eq(funct3_4_eq));  // open: gt, lt
  Comparator #(.Bits(3)) funct8 (.a(funct3_i_pc), .b(3'b000), .eq(funct8_eq));  // open: gt, lt
  and and_2 (add_sub, funct3_eq, r);
  and and_3 (sub_sra, funct7_eq, r);
  and and_4 (addi, funct3_2_eq, i_arith);
  and and_5 (srli, srli_srai, not_1_out, i_arith);
  and and_6 (lb, funct3_3_eq, i_load);
  and and_7 (jalr, funct3_4_eq, i_jalr);
  and and_8 (ecall_ibreak, funct8_eq, i_pc);
  Comparator #(.Bits(3)) funct3_5 (.a(funct3_r), .b(3'b100), .eq(funct3_5_eq));  // open: gt, lt
  Comparator #(.Bits(3)) funct3_6 (.a(funct3_i_arith), .b(3'b100), .eq(funct3_6_eq));  // open: gt, lt
  and and_9 (sub, sub_sra, r, add_sub);
  and and_10 (add, add_sub, r, not_2_out);
  not not_2 (not_2_out, sub);
  Comparator #(.Bits(3)) funct3_7 (.a(funct3_i_load), .b(3'b001), .eq(funct3_7_eq));  // open: gt, lt
  and and_11 (\xor , funct3_5_eq, r);
  and and_12 (xori, funct3_6_eq, i_arith);
  and and_13 (lh, funct3_7_eq, i_load);
  Comparator #(.Bits(3)) funct3_8 (.a(funct3_r), .b(3'b110), .eq(funct3_8_eq));  // open: gt, lt
  and and_14 (sra, sub_sra, r, srl_sra);
  and and_15 (slr, srl_sra, r, not_3_out);
  not not_3 (not_3_out, sra);
  Comparator #(.Bits(3)) funct3_9 (.a(funct3_i_arith), .b(3'b110), .eq(funct3_9_eq));  // open: gt, lt
  Comparator #(.Bits(3)) funct3_10 (.a(funct3_i_load), .b(3'b010), .eq(funct3_10_eq));  // open: gt, lt
  and and_16 (\or , funct3_8_eq, r);
  and and_17 (ori, funct3_9_eq, i_arith);
  and and_18 (lw, funct3_10_eq, i_load);
  Comparator #(.Bits(3)) funct3_11 (.a(funct3_r), .b(3'b111), .eq(funct3_11_eq));  // open: gt, lt
  Comparator #(.Bits(3)) funct3_12 (.a(funct3_i_arith), .b(3'b111), .eq(funct3_12_eq));  // open: gt, lt
  Comparator #(.Bits(3)) funct3_13 (.a(funct3_i_load), .b(3'b100), .eq(funct3_13_eq));  // open: gt, lt
  and and_19 (\and , funct3_11_eq, r);
  and and_20 (andi, funct3_12_eq, i_arith);
  and and_21 (lbu, funct3_13_eq, i_load);
  Comparator #(.Bits(3)) funct3_14 (.a(funct3_r), .b(3'b001), .eq(funct3_14_eq));  // open: gt, lt
  Comparator #(.Bits(3)) funct3_15 (.a(funct3_i_arith), .b(3'b001), .eq(funct3_15_eq));  // open: gt, lt
  and and_22 (sll, funct3_14_eq, r);
  and and_23 (slli, funct3_15_eq, i_arith);
  Comparator #(.Bits(3)) funct3_16 (.a(funct3_i_load), .b(3'b101), .eq(funct3_16_eq));  // open: gt, lt
  and and_24 (lhu, funct3_16_eq, i_load);
  Comparator #(.Bits(3)) funct3_17 (.a(funct3_r), .b(3'b101), .eq(funct3_17_eq));  // open: gt, lt
  Comparator #(.Bits(3)) funct3_18 (.a(funct3_i_arith), .b(3'b101), .eq(funct3_18_eq));  // open: gt, lt
  and and_25 (srl_sra, funct3_17_eq, r);
  and and_26 (srli_srai, funct3_18_eq, i_arith);
  Comparator #(.Bits(3)) funct3_19 (.a(funct3_r), .b(3'b010), .eq(funct3_19_eq));  // open: gt, lt
  Comparator #(.Bits(3)) funct3_20 (.a(funct3_i_arith), .b(3'b010), .eq(funct3_20_eq));  // open: gt, lt
  and and_27 (slt, funct3_19_eq, r);
  and and_28 (slti, funct3_20_eq, i_arith);
  Comparator #(.Bits(3)) funct3_21 (.a(funct3_r), .b(3'b011), .eq(funct3_21_eq));  // open: gt, lt
  Comparator #(.Bits(3)) funct3_22 (.a(funct3_i_arith), .b(3'b011), .eq(funct3_22_eq));  // open: gt, lt
  and and_29 (sltu, funct3_21_eq, r);
  and and_30 (sltiu, funct3_22_eq, i_arith);

  // Other names for the same wires on the sheet: opcode[6:0] = instr[6:0]; resto[24:0] = instr[31:7]
endmodule
