// Digital circuit core.dig as structural Verilog
module core (
  input  clk,
  output [31:0] out
);

  wire and_1_out, branch_1_out, memoOp, need_imm, need_memo, need_write, salta;
  wire [2:0] funct3, immOp;
  wire [3:0] alu_op, BranchOp;
  wire [4:0] rd, rs1, rs2;
  wire [6:0] funct7, opcode;
  wire [31:0] A, B, imm, multiplexer_3_out, multiplexer_4_out, pc_1_out, r1Data, r2Data, sum_s;

  PC pc_1 (.in(multiplexer_3_out), .clk(clk), .out(pc_1_out));
  Add #(.Bits(32)) sum (.a(pc_1_out), .b(32'h4), .c_i(1'b0), .s(sum_s));  // open: c_o
  Insts_Memory insts_memory_1 (.pc(pc_1_out), .out({funct7, rs2, rs1, funct3, rd, opcode}));
  // control_unit control_unit_1: pin names not known; wires that end beside it: opcode, funct3, funct7, alu_op, need_imm, immOp, BranchOp, need_write, salta, memoOp, need_memo
  register_unit register_unit_1 (
    .rdData(out), .rs1(rs1), .rs2(rs2), .rd(rd), .clk(clk), .enable(need_write), .rs1Data(r1Data),
    .rs2Data(r2Data));
  ImmGenerator immgenerator_1 (.inst({funct7, rs2, rs1, funct3, rd}), .ImmOp(immOp), .imm(imm));
  Branch branch_1 (.rs1(r1Data), .rs2(r2Data), .BrOp(BranchOp), .out(branch_1_out));
  and and_1 (and_1_out, need_imm, 1'b1);
  Multiplexer #(.Bits(32)) multiplexer_1 (.sel(salta), .in_0(r1Data), .in_1(pc_1_out), .out(A));
  Multiplexer #(.Bits(32)) multiplexer_2 (.sel(and_1_out), .in_0(r2Data), .in_1(imm), .out(B));
  Multiplexer #(.Bits(32)) multiplexer_3 (.sel(branch_1_out), .in_0(sum_s), .in_1(out), .out(multiplexer_3_out));
  Multiplexer #(.Bits(32)) multiplexer_4 (.sel(need_memo), .in_0(A), .in_1(r2Data), .out(multiplexer_4_out));
  ALU alu_1 (.A(multiplexer_4_out), .B(B), .alu_op(alu_op), .out(out));
  // data_memory data_memory_1: pin names not known; wires that end beside it: out, r1Data, memoOp

  // Other names for the same wires on the sheet: AluOut[31:0] = out
endmodule
